# Fritzing sketch rocket (saved by Fritzing 0.9.6b)
breadboards: 1

parts:
  M1 = RioRand LM2596
  Part1 = Arduino Nano (Rev3.0)
  Mod1 = ossoyoo-lora-module
  BAT1 = Battery Holders [package=lipo-1100mAh]

nets:
  N1: M1.Pin_1, BAT1.+
  N2: M1.Pin_2, BAT1.-
  N3: M1.Pin_3, Part1.VIN
  GND: M1.Pin_4, Part1.GND, Mod1.M0, Mod1.M1, Mod1.GND
  N4: Part1.D1/TX, Mod1.TXD
  N5: Part1.D0/RX, Mod1.RXD

custom parts:
  ossoyoo-lora-module: Osoyoo Long Distance wireless transceiver Uart LoRa Module.
